// Logisim project Processor.circ as structural Verilog: 17 circuits, main circuit Processor
module Processor (
  input  Reset,
  input  Clock,
  input  [7:0] OCA_REG,
  input  [7:0] OCB_REG,
  input  [7:0] PARAM_REG,
  input  [2:0] TIMER_Config_Load,
  input  [7:0] PSC,
  input  [7:0] GPIO_Config_1,
  input  [7:0] GPIO_Config_2,
  input  [7:0] GPIO_Config_3,
  input  [7:0] GPIO_Config_4,
  input  [3:0] GPIO_LOAD_1_4,
  input  ConfigByHand,
  input  [3:0] GPIO_IN_1_4,
  output [2:0] ERRORCode
);

  wire cpu_1_ramstore, GPIO_WE, InstrDiffer, Interrupt, multiplexer_7_out, PWM;
  wire [2:0] InterruptFlags;
  wire [3:0] GPIO_L_1_4, GPIO_OUT_1_4, multiplexer_5_out;
  wire [7:0] GPIO_Conf_1, GPIO_Conf_2, GPIO_Conf_3, GPIO_Conf_4, multiplexer_1_out, multiplexer_2_out,
       multiplexer_3_out, multiplexer_4_out;
  wire [7:3] timerperipheral_1_statusregout;
  wire [11:0] cpu_1_ramaddr, GPIO_RAM_ADDR, multiplexer_6_out;
  wire [15:0] cpu_1_instraddr, cpu_1_ramin, GPIO_DATA, GPIOInstr, instrIn, Instruction, multiplexer_8_out,
       ram_1_dout;

  InstructionROM instructionrom_1 (.InstrAddress(cpu_1_instraddr), .Instruction(Instruction));
  Multiplexer #(.width(8)) multiplexer_1 (
    .in0(GPIO_Conf_1), .in1(GPIO_Config_1), .out(multiplexer_1_out), .sel(ConfigByHand));
  Multiplexer #(.width(8)) multiplexer_2 (
    .in0(GPIO_Conf_2), .in1(GPIO_Config_2), .out(multiplexer_2_out), .sel(ConfigByHand));
  Multiplexer #(.width(8)) multiplexer_3 (
    .in0(GPIO_Conf_3), .in1(GPIO_Config_3), .out(multiplexer_3_out), .sel(ConfigByHand));
  Multiplexer #(.width(8)) multiplexer_4 (
    .in0(GPIO_Conf_4), .in1(GPIO_Config_4), .out(multiplexer_4_out), .sel(ConfigByHand));
  Multiplexer #(.width(4)) multiplexer_5 (
    .in0(GPIO_L_1_4), .in1(GPIO_LOAD_1_4), .out(multiplexer_5_out), .sel(ConfigByHand));
  CPU cpu_1 (
    .instrIn(instrIn), .RAMout(ram_1_dout), .Clock(Clock), .Interrupt(Interrupt),
    .InterruptFlags(InterruptFlags), .Reset(Reset), .RAMin(cpu_1_ramin), .RAMaddr(cpu_1_ramaddr),
    .RAMstore(cpu_1_ramstore), .instrAddr(cpu_1_instraddr), .ERRORCode(ERRORCode));
  TimerPeripheral timerperipheral_1 (
    .OCAdata(OCA_REG), .OCAoverride(TIMER_Config_Load[0]), .OCBdata(OCB_REG),
    .OCBoverride(TIMER_Config_Load[1]), .paramData(PARAM_REG), .PARAMoverride(TIMER_Config_Load[2]),
    .PSC(PSC), .Clock(Clock), .Reset(Reset), .Interrupt(Interrupt), .Waveform1(PWM),
    .StatusRegOut({timerperipheral_1_statusregout, InterruptFlags}));  // open: CNTval
  Comparator #(.width(4)) comparator_1 (.a(Instruction[15:12]), .b(4'b1111), .eq(InstrDiffer));  // open: gt, lt
  Demultiplexer #(.width(16)) demultiplexer_1 (.out0(instrIn), .out1(GPIOInstr), .in(Instruction), .sel(InstrDiffer));
  GPIOPeripheral gpioperipheral_1 (
    .GPIO_REGDATA_1(multiplexer_1_out), .GPIO_REGDATA_2(multiplexer_2_out),
    .GPIO_REGDATA_3(multiplexer_3_out), .GPIO_REGDATA_4(multiplexer_4_out),
    .GPIO_LOAD_1_4(multiplexer_5_out), .GPIO_IN_1_4(GPIO_IN_1_4), .timerIn(PWM), .GPIO_OUT_1_4(GPIO_OUT_1_4));
  Multiplexer #(.width(12)) multiplexer_6 (
    .in0(cpu_1_ramaddr), .in1(GPIO_RAM_ADDR), .out(multiplexer_6_out), .sel(InstrDiffer));
  Multiplexer multiplexer_7 (.in0(cpu_1_ramstore), .in1(GPIO_WE), .out(multiplexer_7_out), .sel(InstrDiffer));
  RAM #(.addrWidth(12), .clearpin("true"), .dataWidth(16), .enables("line")) ram_1 (
    .addr(multiplexer_6_out), .we(multiplexer_7_out), .clk(Clock), .din(multiplexer_8_out),
    .dout(ram_1_dout), .clr(Reset));
  Multiplexer #(.width(16)) multiplexer_8 (
    .in0(cpu_1_ramin), .in1(GPIO_DATA), .out(multiplexer_8_out), .sel(InstrDiffer));
  GPIOHandler gpiohandler_1 (
    .GPIOInstruction(GPIOInstr), .GPIO_OUT(GPIO_OUT_1_4), .GPIO_Config_1(GPIO_Conf_1),
    .GPIO_Config_2(GPIO_Conf_2), .GPIO_Config_3(GPIO_Conf_3), .GPIO_Config_4(GPIO_Conf_4),
    .GPIO_LOAD_1_4(GPIO_L_1_4), .RAMAddr(GPIO_RAM_ADDR), .RAMData(GPIO_DATA), .RAMWriteEnable(GPIO_WE));

  // Other names for the same wires on the sheet: res = Reset

  // Notes on the sheet:
  //   If its a GPIO Instruction, sends zero Instruction to the CPU and sends the Instruction to the GPIO Handler
  //   Differentiates Instruction from GPIO Instruction
  //   Otherwise, the RAM is accessed by the GPIO Handler
  //   If the Instruction does not start with 1111, then the outputs of the CPU Get routed straight to the RAM
endmodule

module CPU (
  input  [15:0] instrIn,
  input  [15:0] RAMout,
  input  Clock,
  input  Interrupt,
  input  [2:0] InterruptFlags,
  input  Reset,
  output [15:0] RAMin,
  output [11:0] RAMaddr,
  output RAMstore,
  output [15:0] instrAddr,
  output [2:0] ERRORCode
);

  wire isrhandler_1_pcloadcom, jmpInstr, jmpmanager_1_pcloadcommand;
  wire [15:0] ALUout, isrhandler_1_pcloadval, JmpRegister, regA, regB, regTemp;

  and and_1 (jmpInstr, instrIn[14], instrIn[15]);
  jmpManager jmpmanager_1 (
    .regTemp(regTemp), .regB(regB), .jmpInstr(jmpInstr), .opCode3opCode4(instrIn[13:12]),
    .PCloadCommand(jmpmanager_1_pcloadcommand));
  registerManager registermanager_1 (
    .ALUout(ALUout), .opCode1(instrIn[15]), .opCode2(instrIn[14]), .opCode3opCode4(instrIn[13:12]),
    .RAMout(RAMout), .Clock(Clock), .resetRegs(Reset), .jumpRegOut(JmpRegister), .regAout(regA),
    .regBout(regB), .RAMin(RAMin), .tempRegOut(regTemp));
  ALU alu_1 (
    .instructALU(instrIn), .inputA(regA), .inputB(regB), .ALUout(ALUout), .zeroDivFlag(ERRORCode[0]),
    .overflowFlag(ERRORCode[1]), .negativeFlag(ERRORCode[2]));
  ISRHandler isrhandler_1 (
    .jumpRegVal(JmpRegister), .PCLoadCommand(jmpmanager_1_pcloadcommand), .InterruptFlags(InterruptFlags),
    .Interrupt(Interrupt), .currPCval(instrAddr), .Clock(Clock), .PCLoadVal(isrhandler_1_pcloadval),
    .PCLoadCom(isrhandler_1_pcloadcom));
  nor nor_1 (RAMstore, instrIn[15], instrIn[14]);
  ProgramCounter programcounter_1 (
    .Clk(Clock), .Reset(Reset), .loadCommand(isrhandler_1_pcloadcom), .loadVal(isrhandler_1_pcloadval),
    .currAddr(instrAddr));

  assign RAMaddr = instrIn[11:0];

  // Other names for the same wires on the sheet: ECode[2:0] = ERRORCode; fullReset = Reset; opCode2 = instrIn[14];
  //   opCode1 = instrIn[15]; opCode3opCode4[1:0] = instrIn[13:12]

  // Notes on the sheet:
  //   0 For MemoryAccess - 1 For CPU Instr
  //   In MemoryAccess Mode, 0 for Store, 1 for Load. In CPU InstrMode,0 For ALU Instr - 1 For JMPInstr
  //   in JMPInstr Mode, 00 JMP - 01 BREQ - 10 BRNE, in all other modes chooses the target/Src register
endmodule

module InstructionROM (
  input  [15:0] InstrAddress,
  output [15:0] Instruction
);

  ROM #(.addrWidth(16), .dataWidth(16)) rom_1 (.addr(InstrAddress), .data(Instruction));

  // Notes on the sheet:
  //   contents of rom_1 (hex, n*v repeats v):
  //   8800 a805 b80e d000 6 8802 9008 1005 9801 4006 8008 5005 b802 c000 63729*0 3001 2002 1003 4 9805
  //   8803 900a 100a 7001 6002 5003 4004
endmodule

module TimerPeripheral (
  input  [7:0] OCAdata,
  input  OCAoverride,
  input  [7:0] OCBdata,
  input  OCBoverride,
  input  [7:0] paramData,
  input  PARAMoverride,
  input  [7:0] PSC,
  input  Clock,
  input  Reset,
  output [7:0] CNTval,
  output Interrupt,
  output Waveform1,
  output [7:0] StatusRegOut
);

  wire ocaW, ocbW, paramW, prescaler_1_prescaledclockout;
  wire [2:0] countermodule_1_ifoca;
  wire [7:0] OCAreg, OCBreg, ParameterRegister_q;

  or or_1 (ocaW, OCAoverride, Clock);
  or or_2 (ocbW, OCBoverride, Clock);
  or or_3 (paramW, PARAMoverride, Clock);
  Register OCARegister (.D(OCAdata), .en(OCAoverride), .clk(ocaW), .Q(OCAreg), .clr(Reset));
  Register OCBRegister (.D(OCBdata), .en(OCBoverride), .clk(ocbW), .Q(OCBreg), .clr(Reset));
  Register ParameterRegister (.D(paramData), .en(PARAMoverride), .clk(paramW), .Q(ParameterRegister_q), .clr(Reset));
  PreScaler prescaler_1 (.PSC(PSC), .Clock(Clock), .PrescaledClockOut(prescaler_1_prescaledclockout));
  CounterModule countermodule_1 (
    .OCA(OCAreg), .OCB(OCBreg), .OIE(ParameterRegister_q[0]), .OCAIE(ParameterRegister_q[1]),
    .OCBIE(ParameterRegister_q[2]), .WaveGenMode(ParameterRegister_q[3]), .Reset(Reset),
    .ClkIn(prescaler_1_prescaledclockout), .CNTVal(CNTval), .IFOCA(countermodule_1_ifoca[0]),
    .IFOCB(countermodule_1_ifoca[1]), .IFO(countermodule_1_ifoca[2]), .Waveform(Waveform1));
  or or_4 (Interrupt, countermodule_1_ifoca[0], countermodule_1_ifoca[1], countermodule_1_ifoca[2]);
  Register StatusRegister (
    .D({{5{1'b0}}, countermodule_1_ifoca}), .en(1'b1), .clk(Clock), .Q(StatusRegOut), .clr(Reset));

  // Other names for the same wires on the sheet: Clk = Clock
endmodule

module GPIOPeripheral (
  input  [7:0] GPIO_REGDATA_1,
  input  [7:0] GPIO_REGDATA_2,
  input  [7:0] GPIO_REGDATA_3,
  input  [7:0] GPIO_REGDATA_4,
  input  [3:0] GPIO_LOAD_1_4,
  input  [3:0] GPIO_IN_1_4,
  input  timerIn,
  output [3:0] GPIO_OUT_1_4
);

  GPIOPinConfig gpiopinconfig_1 (
    .ConfRegData(GPIO_REGDATA_1), .LoadIntoConfReg(GPIO_LOAD_1_4[0]), .GPIO_X_INPUT(GPIO_IN_1_4[0]),
    .TimerPeripheralInput(timerIn), .GPIO_X_OUTPUT(GPIO_OUT_1_4[0]));
  GPIOPinConfig GPIO_Config_2 (
    .ConfRegData(GPIO_REGDATA_2), .LoadIntoConfReg(GPIO_LOAD_1_4[1]), .GPIO_X_INPUT(GPIO_IN_1_4[1]),
    .TimerPeripheralInput(timerIn), .GPIO_X_OUTPUT(GPIO_OUT_1_4[1]));
  GPIOPinConfig GPIO_Config_3 (
    .ConfRegData(GPIO_REGDATA_3), .LoadIntoConfReg(GPIO_LOAD_1_4[2]), .GPIO_X_INPUT(GPIO_IN_1_4[2]),
    .TimerPeripheralInput(timerIn), .GPIO_X_OUTPUT(GPIO_OUT_1_4[2]));
  GPIOPinConfig GPIO_Config_4 (
    .ConfRegData(GPIO_REGDATA_4), .LoadIntoConfReg(GPIO_LOAD_1_4[3]), .GPIO_X_INPUT(GPIO_IN_1_4[3]),
    .TimerPeripheralInput(timerIn), .GPIO_X_OUTPUT(GPIO_OUT_1_4[3]));
endmodule

module GPIOHandler (
  input  [15:0] GPIOInstruction,
  input  [3:0] GPIO_OUT,
  output [7:0] GPIO_Config_1,
  output [7:0] GPIO_Config_2,
  output [7:0] GPIO_Config_3,
  output [7:0] GPIO_Config_4,
  output [3:0] GPIO_LOAD_1_4,
  output [11:0] RAMAddr,
  output [15:0] RAMData,
  output RAMWriteEnable
);

  wire and_1_out, and_2_out, and_3_out, and_4_out;
  wire [15:0] multiplexer_1_out, multiplexer_2_out, multiplexer_3_out, multiplexer_4_out;

  Multiplexer #(.width(16)) multiplexer_1 (
    .in0({16{1'b0}}), .in1({16{1'b1}}), .out(multiplexer_1_out), .sel(and_1_out));
  and and_1 (and_1_out, 1'b1, GPIO_OUT[0]);
  Multiplexer #(.width(16)) multiplexer_2 (
    .in0({16{1'b0}}), .in1({16{1'b1}}), .out(multiplexer_2_out), .sel(and_2_out));
  and and_2 (and_2_out, 1'b1, GPIO_OUT[1]);
  Multiplexer #(.width(16)) multiplexer_3 (
    .in0({16{1'b0}}), .in1({16{1'b1}}), .out(multiplexer_3_out), .sel(and_3_out));
  and and_3 (and_3_out, 1'b1, GPIO_OUT[2]);
  Multiplexer #(.width(16)) multiplexer_4 (
    .in0({16{1'b0}}), .in1({16{1'b1}}), .out(multiplexer_4_out), .sel(and_4_out));
  and and_4 (and_4_out, 1'b1, GPIO_OUT[3]);
  Demultiplexer #(.select(2), .width(8)) demultiplexer_1 (
    .out0(GPIO_Config_1), .out1(GPIO_Config_2), .out2(GPIO_Config_3), .out3(GPIO_Config_4),
    .in(GPIOInstruction[7:0]), .sel(GPIOInstruction[11:10]));
  Multiplexer #(.select(2), .width(16)) multiplexer_5 (
    .in0(multiplexer_1_out), .in1(multiplexer_2_out), .in2(multiplexer_3_out), .in3(multiplexer_4_out),
    .out(RAMData), .sel(GPIOInstruction[11:10]));
  Demultiplexer #(.select(2)) demultiplexer_2 (
    .out0(GPIO_LOAD_1_4[0]), .out1(GPIO_LOAD_1_4[1]), .out2(GPIO_LOAD_1_4[2]), .out3(GPIO_LOAD_1_4[3]),
    .in(GPIOInstruction[9]), .sel(GPIOInstruction[11:10]));
  Multiplexer #(.select(2), .width(12)) multiplexer_6 (
    .in0(12'hffc), .in1(12'hffd), .in2(12'hffe), .in3({12{1'b1}}), .out(RAMAddr), .sel(GPIOInstruction[11:10]));
  not not_1 (RAMWriteEnable, GPIOInstruction[9]);

  // Other names for the same wires on the sheet: R_W = GPIOInstruction[9]; SelectPin[1:0] = GPIOInstruction[11:10]
endmodule

module ALU (
  input  [15:0] instructALU,
  input  [15:0] inputA,
  input  [15:0] inputB,
  output [15:0] ALUout,
  output zeroDivFlag,
  output overflowFlag,
  output negativeFlag
);

  wire arithmunit_1_negativeflag, arithmunit_1_overflowflag, arithmunit_1_zerodivflag;
  wire [15:0] arithmunit_1_arithmout, logicunit_1_logicout, multiplexer_1_out;

  LogicUnit logicunit_1 (.inputA(inputA), .inputB(inputB), .Instr(instructALU[2:0]), .logicOut(logicunit_1_logicout));
  ArithmUnit arithmunit_1 (
    .regA(inputA), .regB(inputB), .arithmInstruction(instructALU[2:0]), .ArithmOut(arithmunit_1_arithmout),
    .zeroDivFlag(arithmunit_1_zerodivflag), .overflowFlag(arithmunit_1_overflowflag),
    .negativeFlag(arithmunit_1_negativeflag));
  and and_1 (zeroDivFlag, arithmunit_1_zerodivflag, instructALU[3]);
  and and_2 (overflowFlag, arithmunit_1_overflowflag, instructALU[3]);
  and and_3 (negativeFlag, arithmunit_1_negativeflag, instructALU[3]);
  Multiplexer #(.width(16)) multiplexer_1 (
    .in0(logicunit_1_logicout), .in1(arithmunit_1_arithmout), .out(multiplexer_1_out), .sel(instructALU[3]));
  Multiplexer #(.width(16)) multiplexer_2 (
    .in0(multiplexer_1_out), .in1({{5{1'b0}}, instructALU[10:0]}), .out(ALUout), .sel(instructALU[11]));

  // Other names for the same wires on the sheet: CONSTgen[10:0] = instructALU[10:0];
  //   logicOrArithmBit = instructALU[3]; CONSTmode = instructALU[11]
endmodule

module ISRHandler (
  input  [15:0] jumpRegVal,
  input  PCLoadCommand,
  input  [2:0] InterruptFlags,
  input  Interrupt,
  input  [15:0] currPCval,
  input  Clock,
  output [15:0] PCLoadVal,
  output PCLoadCom
);

  wire and_1_out, d_ff_1_q, d_ff_2_q, ISREndSignal, ISRMode, or_1_out;
  wire [7:0] counter_1_q;
  wire [15:0] InterruptVectorTable_data, multiplexer_1_out, RA;

  ROM #(.addrWidth(3), .dataWidth(16)) InterruptVectorTable (.addr(InterruptFlags), .data(InterruptVectorTable_data));
  Counter counter_1 (
    .count(1'b1), .Q(counter_1_q), .up(1'b1), .clk(and_1_out), .clr(d_ff_2_q));  // open: load, D, carry
  and and_1 (and_1_out, Clock, ISRMode);
  Register #(.width(16)) u_RA (.D(currPCval), .en(Interrupt), .clk(Interrupt), .Q(RA));  // open: clr
  D_Flip_Flop u_ISRMode (.D(Interrupt), .clk(Interrupt), .Q(ISRMode), .reset(ISREndSignal));  // open: Qn, preset
  Comparator comparator_1 (.a(counter_1_q), .b(8'h32), .eq(ISREndSignal));  // open: gt, lt
  D_Flip_Flop d_ff_1 (.D(1'b1), .clk(ISREndSignal), .Q(d_ff_1_q), .reset(d_ff_2_q));  // open: Qn, preset
  D_Flip_Flop d_ff_2 (.D(d_ff_1_q), .clk(Clock), .Q(d_ff_2_q), .reset(d_ff_2_q));  // open: Qn, preset
  Multiplexer #(.width(16)) multiplexer_1 (
    .in0(InterruptVectorTable_data), .in1(RA), .out(multiplexer_1_out), .sel(ISREndSignal));
  or or_1 (or_1_out, Interrupt, ISREndSignal);
  Multiplexer #(.width(16)) multiplexer_2 (.in0(jumpRegVal), .in1(multiplexer_1_out), .out(PCLoadVal), .sel(or_1_out));
  Multiplexer multiplexer_3 (.in0(PCLoadCommand), .in1(or_1_out), .out(PCLoadCom), .sel(or_1_out));

  // Notes on the sheet:
  //   contents of InterruptVectorTable (hex, n*v repeats v):
  //   0 f8ff f9ff faff fbff fcff fdff feff
endmodule

module jmpManager (
  input  [15:0] regTemp,
  input  [15:0] regB,
  input  jmpInstr,
  input  [1:0] opCode3opCode4,
  output PCloadCommand
);

  wire comparator_1_eq, multiplexer_1_out, not_1_out;

  Comparator #(.width(16)) comparator_1 (.a(regTemp), .b(regB), .eq(comparator_1_eq));  // open: gt, lt
  not not_1 (not_1_out, comparator_1_eq);
  Multiplexer #(.select(2)) multiplexer_1 (
    .in0(1'b1), .in1(comparator_1_eq), .in2(not_1_out), .in3(1'b0), .out(multiplexer_1_out),
    .sel(opCode3opCode4));
  and and_1 (PCloadCommand, multiplexer_1_out, jmpInstr);
endmodule

module registerManager (
  input  [15:0] ALUout,
  input  opCode1,
  input  opCode2,
  input  [1:0] opCode3opCode4,
  input  [15:0] RAMout,
  input  Clock,
  input  resetRegs,
  output [15:0] jumpRegOut,
  output [15:0] regAout,
  output [15:0] regBout,
  output [15:0] RAMin,
  output [15:0] tempRegOut
);

  wire and_1_out, and_2_out, and_3_out, and_4_out, demultiplexer_1_out0, demultiplexer_1_out1,
       demultiplexer_1_out2, demultiplexer_1_out3, multiplexer_2_out, multiplexer_3_out, multiplexer_4_out,
       multiplexer_5_out, nand_1_out, or_1_out;
  wire [15:0] multiplexer_1_out;

  Multiplexer #(.width(16)) multiplexer_1 (.in0(RAMout), .in1(ALUout), .out(multiplexer_1_out), .sel(opCode1));
  nand nand_1 (nand_1_out, opCode2, opCode1);
  Demultiplexer #(.select(2)) demultiplexer_1 (
    .out0(demultiplexer_1_out0), .out1(demultiplexer_1_out1), .out2(demultiplexer_1_out2),
    .out3(demultiplexer_1_out3), .in(1'b1), .sel(opCode3opCode4));
  or or_1 (or_1_out, opCode2, opCode1);
  Multiplexer multiplexer_2 (.in0(1'b0), .in1(demultiplexer_1_out3), .out(multiplexer_2_out), .sel(or_1_out));
  Multiplexer multiplexer_3 (.in0(1'b0), .in1(demultiplexer_1_out2), .out(multiplexer_3_out), .sel(or_1_out));
  Multiplexer multiplexer_4 (.in0(1'b0), .in1(demultiplexer_1_out1), .out(multiplexer_4_out), .sel(or_1_out));
  Multiplexer multiplexer_5 (.in0(1'b0), .in1(demultiplexer_1_out0), .out(multiplexer_5_out), .sel(or_1_out));
  and and_1 (and_1_out, nand_1_out, multiplexer_2_out);
  and and_2 (and_2_out, nand_1_out, multiplexer_3_out);
  and and_3 (and_3_out, nand_1_out, multiplexer_4_out);
  and and_4 (and_4_out, nand_1_out, multiplexer_5_out);
  Register #(.width(16)) regJump (.D(multiplexer_1_out), .en(and_1_out), .clk(Clock), .Q(jumpRegOut), .clr(resetRegs));
  Register #(.width(16)) regTemp (.D(multiplexer_1_out), .en(and_2_out), .clk(Clock), .Q(tempRegOut), .clr(resetRegs));
  Register #(.width(16)) regA (.D(multiplexer_1_out), .en(and_3_out), .clk(Clock), .Q(regAout), .clr(resetRegs));
  Register #(.width(16)) regB (.D(multiplexer_1_out), .en(and_4_out), .clk(Clock), .Q(regBout), .clr(resetRegs));
  Multiplexer #(.select(2), .width(16)) multiplexer_6 (
    .in0(regBout), .in1(regAout), .in2(tempRegOut), .in3(jumpRegOut), .out(RAMin), .sel(opCode3opCode4));

  // Other names for the same wires on the sheet: regA[15:0] = regAout; regB[15:0] = regBout

  // Notes on the sheet:
  //   Target Reg Chooser
  //   AND gates to ensure we are not in JMP mode
  //   SRC Reg Chooser
endmodule

module ProgramCounter (
  input  Clk,
  input  Reset,
  input  loadCommand,
  input  [15:0] loadVal,
  output [15:0] currAddr
);

  Counter #(.max('hffff), .width(16)) InstructionRegister (
    .load(loadCommand), .D(loadVal), .count(1'b1), .Q(currAddr), .clk(Clk), .clr(Reset));  // open: carry, up
endmodule

module ArithmUnit (
  input  [15:0] regA,
  input  [15:0] regB,
  input  [2:0] arithmInstruction,
  output [15:0] ArithmOut,
  output zeroDivFlag,
  output overflowFlag,
  output negativeFlag
);

  wire comparator_1_eq, comparator_2_eq, comparator_3_eq, comparator_4_eq, or_1_out, sumOverflow;
  wire [15:0] adder_1_out, demultiplexer_1_out0, demultiplexer_1_out1, demultiplexer_1_out2,
       demultiplexer_1_out3, demultiplexer_1_out4, demultiplexer_1_out6, demultiplexer_2_out0,
       demultiplexer_2_out1, demultiplexer_2_out2, demultiplexer_2_out3, demultiplexer_2_out4,
       demultiplexer_2_out7, divider_1_out, divider_1_rem, mulOverflow, multiplier_1_out, shifter_1_out,
       subtractor_1_out;

  Demultiplexer #(.select(3), .width(16)) demultiplexer_1 (
    .out0(demultiplexer_1_out0), .out1(demultiplexer_1_out1), .out2(demultiplexer_1_out2),
    .out3(demultiplexer_1_out3), .out4(demultiplexer_1_out4), .out6(demultiplexer_1_out6), .in(regA),
    .sel(arithmInstruction));  // open: out5, out7
  Demultiplexer #(.select(3), .width(16)) demultiplexer_2 (
    .out0(demultiplexer_2_out0), .out1(demultiplexer_2_out1), .out2(demultiplexer_2_out2),
    .out3(demultiplexer_2_out3), .out4(demultiplexer_2_out4), .out7(demultiplexer_2_out7), .in(regB),
    .sel(arithmInstruction));  // open: out5, out6
  Comparator #(.width(3)) comparator_1 (.a(arithmInstruction), .b(3'b011), .eq(comparator_1_eq));  // open: gt, lt
  Comparator #(.width(3)) comparator_2 (.a(arithmInstruction), .b(3'b101), .eq(comparator_2_eq));  // open: gt, lt
  Comparator #(.width(16)) comparator_3 (.a(regB), .b({16{1'b0}}), .eq(comparator_3_eq));  // open: gt, lt
  or or_1 (or_1_out, comparator_1_eq, comparator_2_eq);
  and and_1 (zeroDivFlag, or_1_out, comparator_3_eq);
  Adder #(.width(16)) adder_1 (
    .a(demultiplexer_1_out0), .b(demultiplexer_2_out0), .out(adder_1_out), .cout(sumOverflow));  // open: cin
  Subtractor #(.width(16)) subtractor_1 (
    .a(demultiplexer_1_out1), .b(demultiplexer_2_out1), .out(subtractor_1_out), .bout(negativeFlag));  // open: bin
  Multiplier #(.width(16)) multiplier_1 (
    .a(demultiplexer_1_out2), .b(demultiplexer_2_out2), .out(multiplier_1_out), .cout(mulOverflow));  // open: cin
  Divider #(.width(16)) divider_1 (
    .a(demultiplexer_1_out3), .b(demultiplexer_2_out3), .out(divider_1_out), .rem(divider_1_rem));  // open: upper
  Shifter #(.shift("ar"), .width(16)) shifter_1 (
    .in(demultiplexer_1_out4), .\dist (demultiplexer_2_out4[3:0]), .out(shifter_1_out));
  Comparator #(.width(16)) comparator_4 (.a(mulOverflow), .b({16{1'b0}}), .eq(comparator_4_eq));  // open: gt, lt
  Multiplexer #(.select(3), .width(16)) multiplexer_1 (
    .in0(adder_1_out), .in1(subtractor_1_out), .in2(multiplier_1_out), .in3(divider_1_out),
    .in4(shifter_1_out), .in5(divider_1_rem), .in6(demultiplexer_1_out6), .in7(demultiplexer_2_out7),
    .out(ArithmOut), .sel(arithmInstruction));
  or or_2 (overflowFlag, sumOverflow, comparator_4_eq);

  // Other names for the same wires on the sheet: negative = negativeFlag
endmodule

module LogicUnit (
  input  [15:0] inputA,
  input  [15:0] inputB,
  input  [2:0] Instr,
  output [15:0] logicOut
);

  wire [15:0] and_1_out, demultiplexer_1_out0, demultiplexer_1_out1, demultiplexer_1_out2,
       demultiplexer_1_out3, demultiplexer_1_out4, demultiplexer_1_out5, demultiplexer_1_out6,
       demultiplexer_1_out7, demultiplexer_2_out0, demultiplexer_2_out1, demultiplexer_2_out2,
       demultiplexer_2_out3, demultiplexer_2_out4, demultiplexer_2_out6, demultiplexer_2_out7, nand_1_out,
       nor_1_out, not_1_out, or_1_out, shifter_1_out, shifter_2_out, xor_1_out;

  Demultiplexer #(.select(3), .width(16)) demultiplexer_1 (
    .out0(demultiplexer_1_out0), .out1(demultiplexer_1_out1), .out2(demultiplexer_1_out2),
    .out3(demultiplexer_1_out3), .out4(demultiplexer_1_out4), .out5(demultiplexer_1_out5),
    .out6(demultiplexer_1_out6), .out7(demultiplexer_1_out7), .in(inputA), .sel(Instr));
  Demultiplexer #(.select(3), .width(16)) demultiplexer_2 (
    .out0(demultiplexer_2_out0), .out1(demultiplexer_2_out1), .out2(demultiplexer_2_out2),
    .out3(demultiplexer_2_out3), .out4(demultiplexer_2_out4), .out6(demultiplexer_2_out6),
    .out7(demultiplexer_2_out7), .in(inputB), .sel(Instr));  // open: out5
  assign and_1_out = demultiplexer_1_out0 & demultiplexer_2_out0;  // AND_Gate and_1, 16 bits wide
  assign or_1_out = demultiplexer_1_out1 | demultiplexer_2_out1;  // OR_Gate or_1, 16 bits wide
  assign not_1_out = ~demultiplexer_1_out5;  // NOT_Gate not_1, 16 bits wide
  Shifter #(.width(16)) shifter_1 (.in(demultiplexer_1_out6), .\dist (demultiplexer_2_out6[3:0]), .out(shifter_1_out));
  Shifter #(.shift("lr"), .width(16)) shifter_2 (
    .in(demultiplexer_1_out7), .\dist (demultiplexer_2_out7[3:0]), .out(shifter_2_out));
  assign xor_1_out = demultiplexer_1_out2 ^ demultiplexer_2_out2;  // XOR_Gate xor_1, 16 bits wide
  assign nand_1_out = ~(demultiplexer_1_out3 & demultiplexer_2_out3);  // NAND_Gate nand_1, 16 bits wide
  assign nor_1_out = ~(demultiplexer_1_out4 | demultiplexer_2_out4);  // NOR_Gate nor_1, 16 bits wide
  Multiplexer #(.select(3), .width(16)) multiplexer_1 (
    .in0(and_1_out), .in1(or_1_out), .in2(xor_1_out), .in3(nand_1_out), .in4(nor_1_out), .in5(not_1_out),
    .in6(shifter_1_out), .in7(shifter_2_out), .out(logicOut), .sel(Instr));
endmodule

module CounterModule (
  input  [7:0] OCA,
  input  [7:0] OCB,
  input  OIE,
  input  OCAIE,
  input  OCBIE,
  input  WaveGenMode,
  input  Reset,
  input  ClkIn,
  output [7:0] CNTVal,
  output IFOCA,
  output IFOCB,
  output IFO,
  output Waveform
);

  wire and_1_out, and_2_out, and_3_out, cmpA, cmpB, comparator_1_eq, d_ff_1_q, d_ff_2_q, d_ff_3_q, or_1_out,
       t_ff_1_q;

  Counter counter_1 (.count(1'b1), .Q(CNTVal), .clk(ClkIn), .clr(Reset));  // open: load, D, carry, up
  D_Flip_Flop d_ff_1 (.D(1'b1), .clk(comparator_1_eq), .Q(d_ff_1_q), .reset(d_ff_3_q));  // open: Qn, preset
  Comparator comparator_1 (.a({8{1'b1}}), .b(CNTVal), .eq(comparator_1_eq));  // open: gt, lt
  D_Flip_Flop d_ff_2 (.D(d_ff_1_q), .clk(ClkIn), .Q(d_ff_2_q), .reset(d_ff_3_q));  // open: Qn, preset
  D_Flip_Flop d_ff_3 (.D(d_ff_2_q), .clk(ClkIn), .Q(d_ff_3_q), .reset(d_ff_3_q));  // open: Qn, preset
  Comparator comparator_2 (.a(OCA), .b(CNTVal), .eq(cmpA));  // open: gt, lt
  Comparator comparator_3 (.a(OCB), .b(CNTVal), .eq(cmpB));  // open: gt, lt
  and and_1 (and_1_out, d_ff_2_q, OIE);
  or or_1 (or_1_out, cmpA, cmpB);
  and and_2 (and_2_out, cmpA, OCAIE);
  and and_3 (and_3_out, OCBIE, cmpB);
  T_Flip_Flop t_ff_1 (.T(1'b1), .clk(or_1_out), .Q(t_ff_1_q));  // open: Qn, reset, preset
  TwoTactLatch twotactlatch_1 (.TactIn(ClkIn), .LatchTrig(and_2_out), .LatchOut(IFOCA));
  TwoTactLatch twotactlatch_2 (.TactIn(ClkIn), .LatchTrig(and_3_out), .LatchOut(IFOCB));
  and and_4 (Waveform, t_ff_1_q, WaveGenMode);
  TwoTactLatch twotactlatch_3 (.TactIn(ClkIn), .LatchTrig(and_1_out), .LatchOut(IFO));

  // Other names for the same wires on the sheet: Clk = ClkIn; WaveGen1 = WaveGenMode
endmodule

module PreScaler (
  input  [7:0] PSC,
  input  Clock,
  output PrescaledClockOut
);

  wire comparator_1_eq, comparator_2_eq, comparator_2_lt;
  wire [7:0] counter_1_q;

  Counter counter_1 (.count(1'b1), .Q(counter_1_q), .clk(Clock), .clr(comparator_2_lt));  // open: load, D, carry, up
  Comparator comparator_1 (.a({8{1'b0}}), .b(PSC), .eq(comparator_1_eq));  // open: gt, lt
  Comparator comparator_2 (.a(PSC), .b(counter_1_q), .eq(comparator_2_eq), .lt(comparator_2_lt));  // open: gt
  Multiplexer multiplexer_1 (.in0(comparator_2_eq), .in1(Clock), .out(PrescaledClockOut), .sel(comparator_1_eq));

  // Notes on the sheet:
  //   The Prescaled Clock triggers once every PSC+1 Clock Cycles
endmodule

module TwoTactLatch (
  input  TactIn,
  input  LatchTrig,
  output LatchOut
);

  wire d_ff_2_q, turnOffFlag;

  D_Flip_Flop d_ff_1 (.D(1'b1), .clk(LatchTrig), .Q(LatchOut), .reset(turnOffFlag));  // open: Qn, preset
  D_Flip_Flop d_ff_2 (.D(LatchOut), .clk(TactIn), .Q(d_ff_2_q), .reset(turnOffFlag));  // open: Qn, preset
  D_Flip_Flop d_ff_3 (.D(d_ff_2_q), .clk(TactIn), .Q(turnOffFlag), .reset(turnOffFlag));  // open: Qn, preset
endmodule

module GPIOPinConfig (
  input  [7:0] ConfRegData,
  input  LoadIntoConfReg,
  input  GPIO_X_INPUT,
  input  TimerPeripheralInput,
  output GPIO_X_OUTPUT
);

  wire HighOrLow, Input_Output, multiplexer_1_out, TimerMode;
  wire [7:3] GPIO_Conf_X_q;

  Register GPIO_Conf_X (
    .D(ConfRegData), .en(LoadIntoConfReg), .clk(LoadIntoConfReg),
    .Q({GPIO_Conf_X_q, TimerMode, HighOrLow, Input_Output}));  // open: clr
  Multiplexer multiplexer_1 (.in0(HighOrLow), .in1(TimerPeripheralInput), .out(multiplexer_1_out), .sel(TimerMode));
  Multiplexer multiplexer_2 (.in0(GPIO_X_INPUT), .in1(multiplexer_1_out), .out(GPIO_X_OUTPUT), .sel(Input_Output));
endmodule
